// Logisim project MultRepeatedAdder.circ as structural Verilog: 4 circuits, main circuit main
module main (
  input  [31:0] Input_A,
  input  [31:0] Input_B,
  input  Reset,
  output [31:0] Product,
  output Stall_Pipeline
);

  wire Clock_out;

  Clock Clock (.out(Clock_out));
  Mult mult_1 (
    .A(Input_A), .B(Input_B), .Clock(Clock_out), .Reset(Reset), .Product(Product),
    .Stall_Pipeline(Stall_Pipeline));
endmodule

module Mult (
  input  [31:0] A,
  input  [31:0] B,
  input  Clock,
  input  Reset,
  output [31:0] Product,
  output Stall_Pipeline
);

  wire [31:0] Product_q;

  Register #(.width(32)) u_Product (.D(Product), .en(Stall_Pipeline), .Q(Product_q), .clk(Clock), .clr(Reset));
  Adder #(.width(32)) adder_1 (.a(A), .b(Product_q), .out(Product));  // open: cin, cout
  CountUpTo countupto_1 (.Reset(Reset), .Limit(B), .IsCounting(Stall_Pipeline), .Clock(Clock));

  // Other names for the same wires on the sheet: clk = Clock; shouldStall = Stall_Pipeline

  // Notes on the sheet:
  //   INPUTS
  //   IMPLEMENT A*B
  //   OUTPUTS
endmodule

module CountUpTo (
  input  Reset,
  input  Clock,
  input  [31:0] Limit,
  output IsCounting
);

  wire comparator_1_eq, comparator_1_gt, or_1_out;
  wire [31:0] B_Comp_q, curr;

  Register #(.width(32)) B_Comp (.D(curr), .Q(B_Comp_q), .clk(Clock), .clr(Reset));  // open: en
  Adder #(.width(32)) adder_1 (.a(32'h1), .b(B_Comp_q), .out(curr));  // open: cin, cout
  Comparator #(.width(32), .mode("unsigned")) comparator_1 (
    .a(curr), .b(Limit), .gt(comparator_1_gt), .eq(comparator_1_eq));  // open: lt
  not not_1 (IsCounting, or_1_out);
  or or_1 (or_1_out, comparator_1_gt, comparator_1_eq);

  // Other names for the same wires on the sheet: clk = Clock; rst = Reset

  // Notes on the sheet:
  //   INPUTS
  //   IMPLEMENT
  //   OUTPUTS
endmodule

module Fib (
  input  [31:0] N,
  input  clk,
  input  rst,
  output [31:0] out_4,
  output [31:0] Stopped
);

  wire comparator_1_eq, comparator_1_gt, comparator_1_lt, hold, not_1_out, or_1_out;
  wire [31:0] n_1, n_1_1, n_2, register_3_q;

  Comparator #(.width(32)) comparator_1 (
    .a(n_1_1), .b(32'h1), .gt(comparator_1_gt), .eq(comparator_1_eq), .lt(comparator_1_lt));
  Register #(.width(32)) register_1 (.D(n_1), .Q(n_2), .clk(clk), .clr(rst));  // open: en
  Register #(.width(32)) register_2 (.D(out_4), .Q(n_1_1), .clk(clk), .clr(rst));  // open: en
  CountUpTo countupto_1 (.Reset(rst), .Limit(N), .IsCounting(hold), .Clock(clk));
  Transistor #(.\type ("n"), .gate("br"), .width(32)) transistor_1 (.in(n_1_1), .out(n_1), .gate(or_1_out));
  or or_1 (or_1_out, comparator_1_gt, comparator_1_eq);
  Transistor #(.\type ("n"), .width(32)) transistor_2 (.in(32'h1), .out(n_1), .gate(comparator_1_lt));
  Adder #(.width(32)) adder_1 (.a(n_2), .b(n_1), .out(out_4));  // open: cin, cout
  Register #(.width(32)) register_3 (.D(out_4), .en(hold), .Q(register_3_q), .clk(clk), .clr(rst));
  not not_1 (not_1_out, hold);
  Multiplexer #(.width(32)) multiplexer_1 (
    .in0(out_4), .in1(register_3_q), .out(Stopped), .sel(not_1_out));  // open: en

  // Other names for the same wires on the sheet: count[31:0] = N; n_t[31:0] = out_4
endmodule
