// Logisim project lab7.circ as structural Verilog: 7 circuits, main circuit main
module main (
  input  Input_A,
  input  Switch,
  input  Input_B,
  input  in_4,
  input  in_5,
  input  in_6,
  input  in_7,
  input  in_8,
  input  in_9,
  input  in_10,
  input  in_11,
  input  in_12,
  input  in_13,
  input  in_14,
  input  in_15,
  output [7:0] out_16,
  output out_17,
  output [7:0] out_18,
  output out_19,
  output out_20,
  output out_21,
  output out_22
);

  _2to1MUX u_2to1mux_1 (.Input_A(Input_A), .Switch(Switch), .Input_B(Input_B), .Output(out_17));
  NAND nand_1 (.in_1(in_4), .in_2(in_7), .out_3(out_19));
  NOR nor_1 (.in_1(in_11), .in_2(in_13), .out_3(out_21));
  XOR xor_1 (.in_1(in_14), .in_2(in_15), .out_3(out_22));
  AddMachine addmachine_1 (.out_1(out_16), .out_2(out_18));
  _4to1MUX u_4to1mux_1 (
    .Switch_A(in_6), .Switch_B(in_5), .Input_A(in_8), .Input_B(in_9), .Inpiut_C(in_10), .Input_D(in_12),
    .out_7(out_20));
endmodule

module NAND (
  input  in_1,
  input  in_2,
  output out_3
);

  wire and_1_out;

  and and_1 (and_1_out, in_1, in_2);
  not not_1 (out_3, and_1_out);
endmodule

module NOR (
  input  in_1,
  input  in_2,
  output out_3
);

  wire or_1_out;

  or or_1 (or_1_out, in_1, in_1, in_2);
  not not_1 (out_3, or_1_out);
endmodule

module XOR (
  input  in_1,
  input  in_2,
  output out_3
);

  wire and_1_out, and_2_out, not_1_out, not_2_out, or_1_out;

  and and_1 (and_1_out, in_1, in_1, in_2, in_2);
  not not_1 (not_1_out, in_1);
  not not_2 (not_2_out, in_2);
  and and_2 (and_2_out, not_1_out, not_2_out);
  or or_1 (or_1_out, and_1_out, and_2_out);
  not not_3 (out_3, or_1_out);
endmodule

// 2_1_MUX
module _2to1MUX (
  input  Input_A,
  input  Switch,
  input  Input_B,
  output Output
);

  wire and_1_out, and_2_out, not_1_out;

  not not_1 (not_1_out, Switch);
  and and_1 (and_1_out, Input_A, Switch);
  and and_2 (and_2_out, not_1_out, Input_B);
  or or_1 (Output, and_1_out, and_2_out);
endmodule

// 4_1_MUX
module _4to1MUX (
  input  Switch_A,
  input  Switch_B,
  input  Input_A,
  input  Input_B,
  input  Inpiut_C,
  input  Input_D,
  output out_7
);

  wire and_1_out, and_2_out, and_3_out, and_4_out, not_1_out, not_2_out, not_3_out, not_4_out;

  not not_1 (not_1_out, Switch_B);
  not not_2 (not_2_out, Switch_A);
  not not_3 (not_3_out, Switch_B);
  not not_4 (not_4_out, Switch_A);
  and and_1 (and_1_out, Switch_B, Switch_A, Input_A);
  and and_2 (and_2_out, Switch_A, not_1_out, Input_B);
  and and_3 (and_3_out, not_2_out, Switch_B, Inpiut_C);
  and and_4 (and_4_out, not_3_out, not_4_out, Input_D);
  or or_1 (out_7, and_1_out, and_2_out, and_3_out, and_4_out);
endmodule

module AddMachine (
  output [7:0] out_1,
  output [7:0] out_2
);

  wire clock_1_out;

  Adder adder_1 (.a(8'h1), .b(out_2), .out(out_1));  // open: cin, cout
  Clock clock_1 (.out(clock_1_out));
  Register register_1 (.D(out_1), .Q(out_2), .clk(clock_1_out));  // open: en, clr

  // Notes on the sheet:
  //   weren't showing the value.
  //   They were pointing East... xD
  //   We were confused why my outputs
endmodule
