// Logisim project lab8.circ as structural Verilog: 2 circuits, main circuit Ex1
module Ex1 (
  input  [7:0] Input,
  output Out_1,
  output [7:0] Out_2
);

  and and_1 (Out_1, Input[0], Input[7]);
  not not_1 (Out_2[7], Input[7]);

  assign Out_2[6:0] = Input[6:0];
endmodule

module rotr (
  input  [3:0] Rotate_Amount,
  input  [15:0] Input,
  output [15:0] out_3
);

  wire [3:0] adder_1_out, adder_2_out, adder_3_out, adder_4_out, adder_5_out, adder_6_out, adder_7_out,
       adder_8_out, adder_9_out, adder_10_out, adder_11_out, adder_12_out, adder_13_out, adder_14_out,
       adder_15_out, adder_16_out;

  BitSelector #(.width(16)) bitselector_1 (.in(Input), .out(out_3[15]), .sel(adder_1_out));
  Adder #(.width(4)) adder_1 (.a(Rotate_Amount), .b(4'b1111), .out(adder_1_out));  // open: cin, cout
  BitSelector #(.width(16)) bitselector_2 (.in(Input), .out(out_3[14]), .sel(adder_2_out));
  Adder #(.width(4)) adder_2 (.a(Rotate_Amount), .b(4'b1110), .out(adder_2_out));  // open: cin, cout
  BitSelector #(.width(16)) bitselector_3 (.in(Input), .out(out_3[13]), .sel(adder_3_out));
  Adder #(.width(4)) adder_3 (.a(Rotate_Amount), .b(4'b1101), .out(adder_3_out));  // open: cin, cout
  BitSelector #(.width(16)) bitselector_4 (.in(Input), .out(out_3[12]), .sel(adder_4_out));
  Adder #(.width(4)) adder_4 (.a(Rotate_Amount), .b(4'b1100), .out(adder_4_out));  // open: cin, cout
  BitSelector #(.width(16)) bitselector_5 (.in(Input), .out(out_3[7]), .sel(adder_5_out));
  Adder #(.width(4)) adder_5 (.a(Rotate_Amount), .b(4'b0111), .out(adder_5_out));  // open: cin, cout
  BitSelector #(.width(16)) bitselector_6 (.in(Input), .out(out_3[6]), .sel(adder_6_out));
  Adder #(.width(4)) adder_6 (.a(Rotate_Amount), .b(4'b0110), .out(adder_6_out));  // open: cin, cout
  BitSelector #(.width(16)) bitselector_7 (.in(Input), .out(out_3[5]), .sel(adder_7_out));
  Adder #(.width(4)) adder_7 (.a(Rotate_Amount), .b(4'b0101), .out(adder_7_out));  // open: cin, cout
  BitSelector #(.width(16)) bitselector_8 (.in(Input), .out(out_3[4]), .sel(adder_8_out));
  Adder #(.width(4)) adder_8 (.a(Rotate_Amount), .b(4'b0100), .out(adder_8_out));  // open: cin, cout
  BitSelector #(.width(16)) bitselector_9 (.in(Input), .out(out_3[11]), .sel(adder_9_out));
  Adder #(.width(4)) adder_9 (.a(Rotate_Amount), .b(4'b1011), .out(adder_9_out));  // open: cin, cout
  BitSelector #(.width(16)) bitselector_10 (.in(Input), .out(out_3[10]), .sel(adder_10_out));
  Adder #(.width(4)) adder_10 (.a(Rotate_Amount), .b(4'b1010), .out(adder_10_out));  // open: cin, cout
  BitSelector #(.width(16)) bitselector_11 (.in(Input), .out(out_3[9]), .sel(adder_11_out));
  Adder #(.width(4)) adder_11 (.a(Rotate_Amount), .b(4'b1001), .out(adder_11_out));  // open: cin, cout
  BitSelector #(.width(16)) bitselector_12 (.in(Input), .out(out_3[8]), .sel(adder_12_out));
  Adder #(.width(4)) adder_12 (.a(Rotate_Amount), .b(4'b1000), .out(adder_12_out));  // open: cin, cout
  BitSelector #(.width(16)) bitselector_13 (.in(Input), .out(out_3[3]), .sel(adder_13_out));
  Adder #(.width(4)) adder_13 (.a(Rotate_Amount), .b(4'b0011), .out(adder_13_out));  // open: cin, cout
  BitSelector #(.width(16)) bitselector_14 (.in(Input), .out(out_3[2]), .sel(adder_14_out));
  Adder #(.width(4)) adder_14 (.a(Rotate_Amount), .b(4'b0010), .out(adder_14_out));  // open: cin, cout
  BitSelector #(.width(16)) bitselector_15 (.in(Input), .out(out_3[1]), .sel(adder_15_out));
  Adder #(.width(4)) adder_15 (.a(Rotate_Amount), .b(4'b0001), .out(adder_15_out));  // open: cin, cout
  BitSelector #(.width(16)) bitselector_16 (.in(Input), .out(out_3[0]), .sel(adder_16_out));
  Adder #(.width(4)) adder_16 (.a(Rotate_Amount), .b(4'b0000), .out(adder_16_out));  // open: cin, cout

  // Notes on the sheet:
  //   Bits 15-12
  //   Bits 7-4
  //   Bits 3-0
  //   Bits 11-8
  //   I probably should have made the
  //   4 bit shifter it's own circuit
  //   Live and learn I guess :)
endmodule
