// Logisim project regfile.circ as structural Verilog: 2 circuits, main circuit main
module main (
  input  [2:0] Read_Register_1,
  input  [2:0] Read_Register_2,
  input  [2:0] Write_Register,
  input  [15:0] Write_Data,
  input  Write_Enable,
  input  Clock,
  output [15:0] s0_Value,
  output [15:0] s1_Value,
  output [15:0] s2_Value,
  output [15:0] ra_Value,
  output [15:0] sp_Value,
  output [15:0] Read_Data_1,
  output [15:0] Read_Data_2
);

  wire reg_0_en, reg_1_en, reg_2_en, reg_3_en, reg_4_en, reg_5_en, reg_6_en, reg_7_en;
  wire [15:0] reg_0_out, reg_5_out, reg_6_out;

  Demultiplexer #(.select(3)) demultiplexer_1 (
    .out0(reg_0_en), .out1(reg_1_en), .out2(reg_2_en), .out3(reg_3_en), .out4(reg_4_en), .out5(reg_5_en),
    .out6(reg_6_en), .out7(reg_7_en), .in(Write_Enable), .sel(Write_Register));  // open: en
  Register #(.width(16)) register_1 (.en(reg_0_en), .Q(reg_0_out), .clk(Clock));  // open: D, clr
  Register #(.width(16)) register_2 (.D(Write_Data), .en(reg_3_en), .Q(s1_Value), .clk(Clock));  // open: clr
  Register #(.width(16)) register_3 (.D(Write_Data), .en(reg_6_en), .Q(reg_6_out), .clk(Clock));  // open: clr
  Register #(.width(16)) register_4 (.D(Write_Data), .en(reg_1_en), .Q(ra_Value), .clk(Clock));  // open: clr
  Register #(.width(16)) register_5 (.D(Write_Data), .en(reg_4_en), .Q(s2_Value), .clk(Clock));  // open: clr
  Register #(.width(16)) register_6 (.D(Write_Data), .en(reg_7_en), .Q(sp_Value), .clk(Clock));  // open: clr
  Register #(.width(16)) register_7 (.D(Write_Data), .en(reg_2_en), .Q(s0_Value), .clk(Clock));  // open: clr
  Register #(.width(16)) register_8 (.D(Write_Data), .en(reg_5_en), .Q(reg_5_out), .clk(Clock));  // open: clr
  Multiplexer #(.select(3), .width(16)) multiplexer_1 (
    .in0(reg_0_out), .in1(ra_Value), .in2(s0_Value), .in3(s1_Value), .in4(s2_Value), .in5(reg_5_out),
    .in6(reg_6_out), .in7(sp_Value), .out(Read_Data_1), .sel(Read_Register_1));  // open: en
  Multiplexer #(.select(3), .width(16)) multiplexer_2 (
    .in0(reg_0_out), .in1(ra_Value), .in2(s0_Value), .in3(s1_Value), .in4(s2_Value), .in5(reg_5_out),
    .in6(reg_6_out), .in7(sp_Value), .out(Read_Data_2), .sel(Read_Register_2));  // open: en

  // Other names for the same wires on the sheet: clk = Clock; read_data1[15:0] = Read_Data_1;
  //   read_data2[15:0] = Read_Data_2; read_reg1[2:0] = Read_Register_1; read_reg2[2:0] = Read_Register_2;
  //   reg_1_out[15:0] = ra_Value; reg_2_out[15:0] = s0_Value; reg_3_out[15:0] = s1_Value; reg_4_out[15:0] = s2_Value;
  //   reg_7_out[15:0] = sp_Value; write_en = Write_Enable; write_reg[2:0] = Write_Register

  // Notes on the sheet:
  //   INPUTS to your circuit
  //   Write Selector
  //   DON'T CHANGE THE LOCATIONS OF THE INPUTS AND OUTPUTS!
  //   0 - $0
  //   3 - $s1
  //   6 - $v0
  //   Registers
  //   1 - $ra
  //   4 - $s2
  //   7 - $sp
  //   These are DEBUG/TEST outputs from your circuit.
  //   2 - $s0
  //   5 - $a0
  //   OUTPUTS from your circuit
  //   Read Selector 1
  //   Read Selector 2
endmodule

module wrapped_register (
  input  [15:0] in_1,
  input  [2:0] in_2,
  input  [2:0] in_3,
  output [15:0] out_4
);
endmodule
