// Logisim project alu.circ as structural Verilog: 1 circuit, main circuit main
module main (
  input  [15:0] X,
  input  [15:0] Y,
  input  [2:0] Switch,
  output Equal,
  output [15:0] Result,
  output [15:0] Result_2
);

  wire adder_1_cout, comparator_1_lt;
  wire [3:0] bit_extender_1_out, bit_extender_3_out;
  wire [15:0] op_0_high, op_1_high, op_2_high, op_2_out, op_3_high, op_3_out, op_4_high, op_4_out, op_5_high,
       op_5_out, op_6_high, op_7_high, op_7_out;

  Multiplexer #(.select(3), .width(16)) multiplexer_1 (
    .in0(op_0_high), .in1(op_1_high), .in2(op_2_out), .in3(op_3_out), .in4(op_4_out), .in5(op_5_out),
    .in6(op_6_high), .in7(op_7_out), .out(Result), .sel(Switch));  // open: en
  Bit_Extender #(.in_width(16), .out_width(4)) bit_extender_1 (.in(Y), .out(bit_extender_1_out));
  assign op_3_out = X & Y;  // AND_Gate and_1, 16 bits wide
  Comparator #(.width(16)) comparator_1 (.a(X), .b(Y), .lt(comparator_1_lt));  // open: gt, eq
  Shifter #(.width(16)) shifter_1 (.in(X), .\dist (bit_extender_1_out), .out(op_0_high));
  assign op_6_high = {{15{1'b0}}, comparator_1_lt};  // Bit_Extender bit_extender_2
  Bit_Extender #(.in_width(16), .out_width(4)) bit_extender_3 (.in(Y), .out(bit_extender_3_out));
  assign op_4_out = X | Y;  // OR_Gate or_1, 16 bits wide
  Multiplier #(.width(16)) multiplier_1 (.a(X), .b(Y), .out(op_7_out), .cout(op_7_high));  // open: cin
  Shifter #(.width(16), .shift("lr")) shifter_2 (.in(X), .\dist (bit_extender_3_out), .out(op_1_high));
  Adder #(.width(16)) adder_1 (.a(X), .b(Y), .out(op_2_out), .cout(adder_1_cout));  // open: cin
  Comparator #(.width(16), .mode("unsigned")) comparator_2 (.a(X), .b(Y), .eq(Equal));  // open: gt, lt
  assign op_2_high = {{15{1'b0}}, adder_1_cout};  // Bit_Extender bit_extender_4
  assign op_5_out = X ^ Y;  // XOR_Gate xor_1, 16 bits wide
  Multiplexer #(.select(3), .width(16)) multiplexer_2 (
    .in0(op_0_high), .in1(op_1_high), .in2(op_2_high), .in3(op_3_high), .in4(op_4_high), .in5(op_5_high),
    .in6(op_6_high), .in7(op_7_high), .out(Result_2), .sel(Switch));  // open: en

  // Other names for the same wires on the sheet: op_0_out[15:0] = op_0_high; op_1_out[15:0] = op_1_high;
  //   op_6_out[15:0] = op_6_high; S[2:0] = Switch

  // Notes on the sheet:
  //   Y: pull=down
  //   INPUTS to your circuit
  //   Result Selector
  //   0 - sll
  //   3 - and
  //   6 - slt
  //   DON'T CHANGE THE LOCATIONS OF THE INPUTS AND OUTPUTS!
  //   Operations
  //   1 - srl
  //   4 - or
  //   7 - mult
  //   2 - add
  //   5 - xor
  //   NA - Equal
  //   OUTPUTS from your circuit
  //   Result 2 Selector
endmodule
