// Logisim project regfile-insert.circ as structural Verilog: 1 circuit, main circuit main
module main (
  output [7:0] test_num,
  output [15:0] s0_Value,
  output [15:0] s1_Value,
  output [15:0] s2_Value,
  output [15:0] ra_Value,
  output [15:0] sp_Value,
  output halt,
  output [15:0] Read_Data_1,
  output [15:0] Read_Data_2
);

  wire clock_1_out;
  wire [7:0] adder_1_out;
  wire [9:0] rom_2_data;
  wire [15:0] WriteData;

  Register register_1 (.D(adder_1_out), .en(1'b1), .Q(test_num), .clk(clock_1_out));  // open: clr
  Adder adder_1 (.a(8'h1), .b(test_num), .out(adder_1_out));  // open: cin, cout
  Comparator #(.mode("unsigned")) comparator_1 (.a(8'h5), .b(test_num), .eq(halt));  // open: gt, lt
  ROM #(.dataWidth(16)) rom_1 (.addr(test_num), .data(WriteData));  // open: sel
  ROM #(.dataWidth(10)) rom_2 (.addr(test_num), .data(rom_2_data), .sel(1'b1));
  Clock clock_1 (.out(clock_1_out));
  regfile_main main_1 (
    .Read_Register_1(rom_2_data[2:0]), .Read_Register_2(rom_2_data[5:3]), .Write_Register(rom_2_data[8:6]),
    .Write_Data(WriteData), .Write_Enable(rom_2_data[9]), .Clock(clock_1_out), .Read_Data_1(Read_Data_1),
    .Read_Data_2(Read_Data_2), .s0_Value(s0_Value), .s1_Value(s1_Value), .s2_Value(s2_Value),
    .ra_Value(ra_Value), .sp_Value(sp_Value));

  // Notes on the sheet:
  //   contents of rom_1 (hex, n*v repeats v):
  //   beef bad f00d 5678 5678
  //   contents of rom_2 (hex, n*v repeats v):
  //   280 2d0 313 63 263
  //   YOUR REGFILE SHOULD FIT IN HERE!
  //   There should be no blue/red wires here, and the result shouldn't be x's.
endmodule
