// Logisim project cpu.circ as structural Verilog: 1 circuit, main circuit main
module main (
  input  [15:0] INSTRUCTION,
  input  CLOCK,
  output [15:0] FETCH_ADDRESS,
  output [15:0] s0_Value,
  output [15:0] s1_Value,
  output [15:0] s2_Value,
  output [15:0] ra_Value,
  output [15:0] sp_Value,
  output [15:0] HI_Value,
  output [15:0] LO_Value
);

  wire and_2_out, and_3_out, and_4_out, br, comparator_2_lt, comparator_3_eq, comparator_5_eq,
       comparator_6_eq, comparator_7_eq, comparator_9_eq, comparator_10_eq, comparator_11_eq, enable_ram,
       enable_write, equal, ins_nop, MEM_p1, MEM_p2, MEM_p7, MEM_p11, nop, not_1_out, or_3_out,
       reg_write_reg, sequal;
  wire [1:0] alu_src, bit_extender_1_out, hi_lo_select, pc_src;
  wire [2:0] alu_op, bit_extender_2_out, i_rd, i_rs, multiplexer_7_out, multiplexer_8_out, reg_data_src;
  wire [5:0] i_imm;
  wire [15:0] adder_1_out, and_1_out, imm_0, imm_sign, imm_u, imm_up, jump_addr, main_1_read_data_1,
       mem_result, multiplexer_9_out, multiplexer_10_out, multiplexer_11_out, multiplexer_12_out,
       multiplexer_13_out, multiplexer_15_out, PC_eq, PC_eqs, PC_neq, pc_plus_2, read_2, register_1_q,
       register_2_q, result, result_2;
  wire [15:12] INSTRUCTION_P;

  Comparator #(.width(4), .mode("unsigned")) comparator_1 (
    .a(INSTRUCTION_P), .b(4'b0010), .eq(reg_write_reg));  // open: gt, lt
  Comparator #(.width(3), .mode("unsigned")) comparator_2 (
    .a(i_imm[2:0]), .b(3'b111), .lt(comparator_2_lt));  // open: gt, eq
  Multiplexer #(.select(4)) multiplexer_1 (
    .in0(comparator_2_lt), .in1(1'b0), .in2(1'b1), .in3(1'b1), .in4(1'b0), .in5(1'b0), .in6(1'b1),
    .in7(1'b1), .in8(1'b1), .in9(1'b1), .in10(1'b1), .in11(1'b0), .in12(1'b1), .in13(1'b1), .in14(1'b0),
    .in15(1'b0), .out(enable_write), .sel(INSTRUCTION_P));  // open: en
  Multiplexer #(.select(4), .width(3)) multiplexer_2 (
    .in0(3'b000), .in1(3'b000), .in2(3'b010), .in3(3'b010), .in4(3'b000), .in5(3'b000), .in6(3'b000),
    .in7(3'b000), .in8(3'b000), .in9(3'b000), .in10(3'b001), .in11(3'b000), .in12(3'b011), .in13(3'b100),
    .in14(3'b000), .in15(3'b000), .out(reg_data_src), .sel(INSTRUCTION_P));  // open: en
  Multiplexer #(.select(4), .width(3)) multiplexer_3 (
    .in0(i_imm[2:0]), .in3(3'b010), .in6(3'b010), .in7(3'b110), .in8(3'b011), .in9(3'b100), .in10(3'b010),
    .in11(3'b010), .out(alu_op), .sel(INSTRUCTION_P));  // open: in1, in2, in4, in5, in12, in13, in14, in15, en
  Multiplexer #(.select(4), .width(2)) multiplexer_4 (
    .in0(2'b00), .in1(2'b00), .in2(2'b01), .in3(2'b10), .in4(2'b11), .in5(2'b11), .in6(2'b00), .in7(2'b00),
    .in8(2'b00), .in9(2'b00), .in10(2'b00), .in11(2'b00), .in12(2'b00), .in13(2'b00), .in14(2'b00),
    .in15(2'b00), .out(pc_src), .sel(INSTRUCTION_P));  // open: en
  Comparator #(.width(3), .mode("unsigned")) comparator_3 (
    .a(i_imm[2:0]), .b(3'b111), .eq(comparator_3_eq));  // open: gt, lt
  Multiplexer #(.select(4), .width(2)) multiplexer_5 (
    .in0(2'b00), .in3(2'b10), .in4(2'b00), .in5(2'b00), .in6(2'b10), .in7(2'b10), .in8(2'b01), .in9(2'b01),
    .in10(2'b10), .in11(2'b10), .out(alu_src), .sel(INSTRUCTION_P));  // open: in1, in2, in12, in13, in14, in15, en
  Comparator #(.width(4), .mode("unsigned")) comparator_4 (
    .a(INSTRUCTION_P), .b(4'b0101), .eq(sequal));  // open: gt, lt
  Comparator #(.width(4), .mode("unsigned")) comparator_5 (
    .a(INSTRUCTION_P), .b(4'b0100), .eq(comparator_5_eq));  // open: gt, lt
  Comparator #(.width(4), .mode("unsigned")) comparator_6 (
    .a(INSTRUCTION_P), .b(4'b0101), .eq(comparator_6_eq));  // open: gt, lt
  Comparator #(.width(4), .mode("unsigned")) comparator_7 (
    .a(INSTRUCTION_P), .b(4'b1011), .eq(comparator_7_eq));  // open: gt, lt
  assign bit_extender_1_out = {{1{1'b0}}, comparator_3_eq};  // Bit_Extender bit_extender_1
  Multiplexer #(.select(4), .width(2)) multiplexer_6 (
    .in0(bit_extender_1_out), .in1(2'b10), .in2(2'b00), .in3(2'b00), .in4(2'b00), .in5(2'b00), .in6(2'b00),
    .in7(2'b00), .in8(2'b00), .in9(2'b00), .in10(2'b00), .in11(2'b00), .in12(2'b00), .in13(2'b00),
    .in14(2'b00), .in15(2'b00), .out(hi_lo_select), .sel(INSTRUCTION_P));  // open: en
  assign bit_extender_2_out = {{1{1'b0}}, i_rd[2:1]};  // Bit_Extender bit_extender_2
  or or_1 (br, comparator_5_eq, comparator_6_eq, comparator_7_eq);
  Multiplexer #(.width(3)) multiplexer_7 (.in0(i_imm[5:3]), .in1(i_rd), .out(multiplexer_7_out), .sel(br));  // open: en
  Multiplexer #(.width(3)) multiplexer_8 (
    .in0(i_rd), .in1(bit_extender_2_out), .out(multiplexer_8_out), .sel(reg_write_reg));  // open: en
  Multiplexer #(.select(3), .width(16)) multiplexer_9 (
    .in0(result), .in1(mem_result), .in2(FETCH_ADDRESS), .in3(HI_Value), .in4(LO_Value),
    .out(multiplexer_9_out), .sel(reg_data_src));  // open: in5, in6, in7, en
  Comparator #(.width(4), .mode("unsigned")) comparator_8 (
    .a(INSTRUCTION_P), .b(4'b1011), .eq(enable_ram));  // open: gt, lt
  regfile_main main_1 (
    .Read_Register_1(i_rs), .Read_Register_2(multiplexer_7_out), .Write_Register(multiplexer_8_out),
    .Write_Data(multiplexer_9_out), .Write_Enable(enable_write), .Clock(CLOCK),
    .Read_Data_1(main_1_read_data_1), .Read_Data_2(read_2), .s0_Value(s0_Value), .s1_Value(s1_Value),
    .s2_Value(s2_Value), .ra_Value(ra_Value), .sp_Value(sp_Value));
  Multiplexer #(.select(2), .width(16)) multiplexer_10 (
    .in0(read_2), .in1(imm_0), .in2(imm_sign), .in3(pc_plus_2), .out(multiplexer_10_out), .sel(alu_src));  // open: en
  Register #(.width(16)) register_1 (.D(FETCH_ADDRESS), .Q(register_1_q), .clk(CLOCK));  // open: en, clr
  alu_main main_2 (
    .Switch(alu_op), .X(main_1_read_data_1), .Equal(equal), .Result(result), .Y(multiplexer_10_out),
    .Result_2(result_2));
  assign imm_0 = {{10{1'b0}}, i_imm};  // Bit_Extender bit_extender_3
  assign imm_sign = {{10{i_imm[5]}}, i_imm};  // Bit_Extender bit_extender_4
  Multiplexer #(.select(2), .width(16)) multiplexer_11 (
    .in0(pc_plus_2), .in1(jump_addr), .in2(result), .in3(PC_eqs), .out(multiplexer_11_out), .sel(pc_src));  // open: en
  Adder #(.width(16)) adder_1 (.a(register_1_q), .b(imm_sign), .out(adder_1_out));  // open: cin, cout
  Multiplexer #(.select(2), .width(16)) multiplexer_12 (
    .in0(HI_Value), .in1(result_2), .in2(HI_Value), .out(multiplexer_12_out), .sel(hi_lo_select));  // open: in3, en
  Register #(.width(16)) HI (.D(multiplexer_12_out), .Q(HI_Value), .clk(CLOCK));  // open: en, clr
  Register #(.width(16)) register_2 (.D(INSTRUCTION), .Q(register_2_q), .clk(CLOCK));  // open: en, clr
  Register #(.width(1)) register_3 (.D(ins_nop), .Q(nop), .clk(CLOCK));  // open: en, clr
  Multiplexer #(.width(16)) multiplexer_13 (
    .in0(multiplexer_11_out), .in1(pc_plus_2), .out(multiplexer_13_out), .sel(nop));  // open: en
  Register #(.width(16)) PC (.D(multiplexer_13_out), .Q(FETCH_ADDRESS), .clk(CLOCK));  // open: en, clr
  // mem_main MEM: pin names not known; wires that end beside it: MEM_p1, MEM_p2, MEM_p2, result, read_2, enable_ram, MEM_p7, CLOCK, MEM_p7, mem_result, MEM_p11
  assign and_1_out = FETCH_ADDRESS & 16'hfc00;  // AND_Gate and_1, 16 bits wide
  Adder #(.width(16)) adder_2 (.a(FETCH_ADDRESS), .b(16'h2), .out(pc_plus_2));  // open: cin, cout
  Multiplexer #(.width(16)) multiplexer_14 (
    .in0(adder_1_out), .in1(pc_plus_2), .out(PC_eq), .sel(not_1_out));  // open: en
  not not_1 (not_1_out, equal);
  Multiplexer #(.select(2), .width(16)) multiplexer_15 (
    .in0(LO_Value), .in1(result), .in2(imm_up), .out(multiplexer_15_out), .sel(hi_lo_select));  // open: in3, en
  Multiplexer #(.width(16)) multiplexer_16 (
    .in0(register_2_q), .in1({16{1'b0}}), .out({INSTRUCTION_P, i_rd, i_rs, i_imm}), .sel(nop));  // open: en
  assign imm_u = {{6{1'b0}}, {i_rd[0], i_rs, i_imm}};  // Bit_Extender bit_extender_5
  Shifter #(.width(16)) shifter_1 (.in(imm_u), .\dist (4'b0110), .out(imm_up));
  Register #(.width(16)) LO (.D(multiplexer_15_out), .Q(LO_Value), .clk(CLOCK));  // open: en, clr
  assign jump_addr = and_1_out | imm_u;  // OR_Gate or_2, 16 bits wide
  Multiplexer #(.width(16)) multiplexer_17 (
    .in0(pc_plus_2), .in1(adder_1_out), .out(PC_neq), .sel(not_1_out));  // open: en
  Multiplexer #(.width(16)) multiplexer_18 (.in0(PC_eq), .in1(PC_neq), .out(PC_eqs), .sel(sequal));  // open: en
  Comparator #(.width(2)) comparator_9 (.a(pc_src), .b(2'b01), .eq(comparator_9_eq));  // open: gt, lt
  Comparator #(.width(2)) comparator_10 (.a(pc_src), .b(2'b10), .eq(comparator_10_eq));  // open: gt, lt
  and and_2 (and_2_out, equal, ~sequal);  // AND_Gate
  or or_3 (or_3_out, and_2_out, and_3_out);
  and and_3 (and_3_out, ~equal, sequal);  // AND_Gate
  or or_4 (ins_nop, comparator_9_eq, comparator_10_eq, and_4_out);
  and and_4 (and_4_out, or_3_out, comparator_11_eq);
  Comparator #(.width(2)) comparator_11 (.a(pc_src), .b(2'b11), .eq(comparator_11_eq));  // open: gt, lt

  // Other names for the same wires on the sheet: clk = CLOCK; fetch_addr[15:0] = FETCH_ADDRESS;
  //   INSTRUCTION_P[11:0] = {i_rd, i_rs, i_imm}; j_func[2:0] = i_imm[2:0]; u_imm[9:0] = {i_rd[0], i_rs, i_imm};
  //   j_rt[2:0] = i_imm[5:3]; j_rs[2:0] = i_rs; j_rd[2:0] = i_rd; u_rd[1:0] = i_rd[2:1]; opcode[3:0] = INSTRUCTION_P;
  //   r_hi[15:0] = HI_Value; r_low[15:0] = LO_Value; ra[15:0] = ra_Value; s0[15:0] = s0_Value; s1[15:0] = s1_Value;
  //   s2[15:0] = s2_Value; sp[15:0] = sp_Value

  // Notes on the sheet:
  //   U-Type
  //   ALU Result
  //   PC + 2
  //   MEM Result
  //   HI
  //   LOW
  //   PC+2
  //   Jump Addr
  //   sequal
  //   Result
  //   Output
  //   Instruction Decoder
  //   These are outputs/inputs from run.circ
  //   I-Type
  //   Inputs
  //   R-Type
  //   Read 2
  //   IMM Sign
  //   IMM 0
  //   These are DEBUG/TEST outputs from your circuit.
  //   Registers/PC Logic
  //   immediates
endmodule
